# Fritzing sketch common-collector-1-fritz (saved by Fritzing 0.9.3b)
breadboards: 1

parts:
  R1 = Resistor [tolerance=±5% resistance=100k package=THT]
  R2 = Trimmer Potentiometer [maximum_resistance=10kΩ package=THT]
  Q1 = NPN-Transistor [package="TO92 [THT]"]
  LED1 = LED - 5mm [color="Red (633nm)" package="5 mm [THT]"]
  R3 = Resistor [tolerance=±5% resistance=510 package=THT]
  VCC1 = 4 x AAA Battery Mount

nets:
  N1: R1.Pin_0, Q1.B
  N2: R2.leg1, R2.wiper, LED1.cathode, VCC1.-
  N3: R2.leg2, VCC1.+
  N4: Q1.E, R3.Pin_1
  N5: LED1.anode, R3.Pin_0

notes:
  [GROUND]
  [Test Point 1
  Base Voltage]
  [Test Point 2
  Collector Voltage]
